# Fritzing sketch cuatudong (saved by Fritzing 0.9.9b)
breadboards: 1

parts:
  Mod1 = KY-032 IR Obstacle Avoidance Sensor Module [package="Breakout board"]
  Part1 = Arduino Uno (Rev3)
  Mod2 = KY-032 IR Obstacle Avoidance Sensor Module [package="Breakout board"]
  L298N1 = L298N DC motor driver
  M1 = DC Motor
  M2 = LJ18A3-H-ZBX [package=THT]
  M3 = LJ18A3-H-ZBX [package=THT]
  SEN1 = US-100 Ultrasonic Distance Sensor  # not connected

nets:
  GND: Mod1.GND, Part1.GND, Mod2.GND, L298N1.GND, M2.VO_(BLU), M3.VO_(BLU)
  N1: Mod1.+, Part1.5V, Mod2.+, L298N1.5V#7, M2.VI_(BRN), M3.VI_(BRN)
  N2: Mod1.out, Part1.D2
  N3: Part1.D8, L298N1.5V#9, L298N1.ENA
  N4: Part1.D3_PWM, Mod2.out
  N5: Part1.D4, M2.SIG_(BLK)
  N6: Part1.D5_PWM, M3.SIG_(BLK)
  N7: Part1.D6_PWM, L298N1.IN1
  N8: Part1.D7, L298N1.IN2
  N9: L298N1.OUT1, M1.pin_2
  N10: L298N1.OUT2, M1.pin_1

custom parts:
  KY-032 IR Obstacle Avoidance Sensor Module: KY-032 Infrared Obstacle Avoidance Sensor. Distance-adjustable, infrared proximity sensor designed for wheeled robots. Also known as AD-032.
  L298N DC motor driver: 2x DC motor driver with 78M05 positive voltage regulator (7..35 V) L298N: max 46 V, 2 A Set 5 V Enable jumper to enable 5 V regultor (needed for the L298N) and +5 V output at screw terminal or supply external +5 V at screw terminal Set ENA and/or ENB to +5 V to enable motor permanently or supply ENA and/or ENB with PWM signal IN1 and IN2 set rotation directory for motor A (OUT1/OUT2) IN2 and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
  LJ18A3-H-ZBX: LJ18A3-H-ZBX Proximity Sensor module.
